// Logisim project d-flip-flop.circ as structural Verilog: 1 circuit, main circuit main
module main (
  input  D,
  input  Clock,
  output Q,
  output minus_Q
);

  wire nand_1_out, nand_2_out, not_1_out;

  not not_1 (not_1_out, D);
  nand nand_1 (nand_1_out, D, Clock);
  nand nand_2 (nand_2_out, not_1_out, Clock);
  nand nand_3 (Q, nand_1_out, minus_Q);
  nand nand_4 (minus_Q, Q, nand_2_out);
endmodule
