// Logisim project jk-flip-flop.circ as structural Verilog: 1 circuit, main circuit main
module main (
  input  J,
  input  clk,
  input  K,
  output Q,
  output minus_Q
);

  wire nand_1_out, nand_2_out;

  nand nand_1 (nand_1_out, minus_Q, J, clk);
  nand nand_2 (nand_2_out, clk, K, Q);
  nand nand_3 (Q, nand_1_out, minus_Q);
  nand nand_4 (minus_Q, Q, nand_2_out);
endmodule
