// Logisim project t-flip-flop.circ as structural Verilog: 1 circuit, main circuit main
module main (
  input  T,
  input  clk,
  output Q,
  output minus_Q
);

  wire and_1_out, and_2_out;

  and and_1 (and_1_out, Q, T, clk);
  and and_2 (and_2_out, clk, T, minus_Q);
  nor nor_1 (Q, and_1_out, minus_Q);
  nor nor_2 (minus_Q, Q, and_2_out);
endmodule
